// Logisim project version1.circ as structural Verilog: 2 circuits, main circuit main
module main (
  input  A,
  input  B,
  input  E,
  output Valid,
  output Direction
);


  // Notes on the sheet:
  //   Enable:  
  //   Asserted: When disk spinning at full speed
  //   Held low when disk is stopped or changing direction
endmodule

module encoder (
  input  E,
  input  A,
  input  B,
  output D,
  output V
);

  wire and_1_out, and_2_out, and_3_out, and_4_out, and_5_out, and_6_out, clock_1_out, not_1_out, not_2_out,
       or_1_out, or_2_out, or_3_out, Q0_q, Q0_qn, Q1_qn;

  Clock clock_1 (.out(clock_1_out));
  not not_1 (not_1_out, A);
  not not_2 (not_2_out, B);
  and and_1 (and_1_out, Q1_qn, E, not_1_out, not_2_out);
  or or_1 (or_1_out, A, B);
  and and_2 (and_2_out, E, V, Q0_qn);
  and and_3 (and_3_out, B, E, A, Q1_qn, Q0_q);
  and and_4 (and_4_out, E, Q0_q);
  and and_5 (and_5_out, and_4_out, or_1_out);
  and and_6 (and_6_out, V, E);
  or or_2 (or_2_out, and_2_out, and_1_out, and_3_out);
  D_Flip_Flop Q1 (.D(or_3_out), .clk(clock_1_out), .Q(V), .Qn(Q1_qn));  // open: preset, reset
  or or_3 (or_3_out, and_5_out, and_6_out);
  D_Flip_Flop Q0 (.D(or_2_out), .clk(clock_1_out), .Q(Q0_q), .Qn(Q0_qn));  // open: preset, reset
  and and_7 (D, V, Q0_q);

  // Notes on the sheet:
  //   On if CW
endmodule
