// Logisim project lab7.circ as structural Verilog: 1 circuit, main circuit main
module main (
  input  I,
  output out_2
);

  wire and_2_out, and_3_out, and_4_out, and_5_out, clock_1_out, nand_1_out, not_1_out, or_1_out, Q0_q, Q1_q,
       Q1_qn, Q2_q, Q2_qn, xor_1_out;

  Clock clock_1 (.out(clock_1_out));
  not not_1 (not_1_out, I);
  D_Flip_Flop Q2 (.D(I), .clk(clock_1_out), .Q(Q2_q), .Qn(Q2_qn));  // open: preset, reset
  D_Flip_Flop Q1 (.D(nand_1_out), .clk(clock_1_out), .Q(Q1_q), .Qn(Q1_qn));  // open: preset, reset
  D_Flip_Flop Q0 (.D(or_1_out), .clk(clock_1_out), .Q(Q0_q));  // open: Qn, preset, reset
  xor xor_1 (xor_1_out, Q2_q, Q0_q);
  and and_1 (out_2, xor_1_out, Q1_q);
  and and_2 (and_2_out, Q0_q, Q1_qn, Q2_qn, I);
  and and_3 (and_3_out, Q2_q, not_1_out);
  and and_4 (and_4_out, and_3_out, Q0_q);
  and and_5 (and_5_out, Q1_q, Q2_qn);
  nand nand_1 (nand_1_out, ~and_2_out, ~and_3_out);  // NAND_Gate
  or or_1 (or_1_out, and_4_out, and_5_out);
endmodule
