// Logisim project Lab9.circ as structural Verilog: 2 circuits, main circuit main
module main (
  input  Func,
  input  Pwr,
  output [2:0] HL,
  output [2:0] FL
);

  wire clock_1_out;
  wire [2:0] register_1_q, register_2_q, shifter_1_out, shifter_2_out;

  Clock clock_1 (.out(clock_1_out));
  Shifter #(.shift("rl"), .width(3)) shifter_1 (.in(HL), .\dist (2'b01), .out(shifter_1_out));
  Shifter #(.shift("rl"), .width(3)) shifter_2 (.in(FL), .\dist (2'b01), .out(shifter_2_out));
  Register #(.width(3)) register_1 (.D(shifter_1_out), .en(Pwr), .clk(clock_1_out), .Q(register_1_q));  // open: clr
  Register #(.width(3)) register_2 (.D(shifter_2_out), .en(Pwr), .clk(clock_1_out), .Q(register_2_q));  // open: clr
  Multiplexer #(.width(3)) multiplexer_1 (.in0(3'b001), .in1(register_1_q), .out(HL), .sel(Func));
  Multiplexer #(.width(3)) multiplexer_2 (.in0(3'b100), .in1(register_2_q), .out(FL), .sel(Func));
  LED led_1 (.in(HL[0]));
  LED led_2 (.in(HL[1]));
  LED led_3 (.in(HL[2]));
  LED led_4 (.in(FL[0]));
  LED led_5 (.in(FL[1]));
  LED led_6 (.in(FL[2]));
endmodule

module version2 (
  input  CHNGE,
  output [2:0] FRL,
  output [2:0] HWL
);

  wire clock_1_out, not_1_out;
  wire [2:0] FR_q, HW_q, shifter_1_out;

  Clock clock_1 (.out(clock_1_out));
  Shifter #(.shift("rl"), .width(3)) shifter_1 (.in(FRL), .\dist (2'b01), .out(shifter_1_out));
  Register #(.width(3)) FR (.D(shifter_1_out), .en(CHNGE), .clk(clock_1_out), .Q(FR_q));  // open: clr
  Register #(.width(3)) HW (.D(HWL), .en(CHNGE), .clk(clock_1_out), .Q(HW_q));  // open: clr
  Multiplexer #(.width(3)) multiplexer_1 (.in0(3'b100), .in1(FR_q), .out(FRL), .sel(not_1_out));
  not not_1 (not_1_out, CHNGE);
  Multiplexer #(.width(3)) multiplexer_2 (.in0(3'b001), .in1(HW_q), .out(HWL), .sel(CHNGE));
  LED led_1 (.in(FRL[0]));
  LED led_2 (.in(FRL[1]));
  LED led_3 (.in(FRL[2]));
  LED led_4 (.in(HWL[0]));
  LED led_5 (.in(HWL[1]));
  LED led_6 (.in(HWL[2]));
endmodule
