// Logisim project Lab_11.circ as structural Verilog: 2 circuits, main circuit RegFile
module RegFile (
  input  [3:0] D_IN,
  input  RW,
  input  [2:0] DA,
  input  CLK,
  input  [2:0] AA,
  input  [2:0] BA,
  output [3:0] A_OUT,
  output [3:0] B_OUT,
  output [3:0] AOut,
  output [3:0] BOut
);

  wire and_1_out, and_2_out, and_3_out, and_4_out, and_5_out, and_6_out, and_7_out, and_8_out, and_9_out,
       and_10_out, and_11_out, and_12_out, and_13_out, and_14_out, and_15_out, and_16_out, decoder_1_out0,
       decoder_1_out1, decoder_1_out2, decoder_1_out3, decoder_1_out4, decoder_1_out5, decoder_1_out6,
       decoder_1_out7, decoder_2_out0, decoder_2_out1, decoder_2_out2, decoder_2_out3, decoder_2_out4,
       decoder_2_out5, decoder_2_out6, decoder_2_out7;
  wire [3:0] R0_q, R1_q, R2_q, R3_q, R4_q, R5_q, R6_q, R7_q, register_1_q, register_2_q, register_3_q,
       register_4_q, register_5_q, register_6_q, register_7_q, register_8_q;

  Decoder #(.enable("false"), .select(3)) decoder_1 (
    .out0(decoder_1_out0), .out1(decoder_1_out1), .out2(decoder_1_out2), .out3(decoder_1_out3),
    .out4(decoder_1_out4), .out5(decoder_1_out5), .out6(decoder_1_out6), .out7(decoder_1_out7), .sel(DA));
  Register #(.width(4)) R0 (.D(D_IN), .en(and_1_out), .clk(CLK), .Q(R0_q));  // open: clr
  buf and_1 (and_1_out, decoder_1_out0);  // AND_Gate
  Register #(.width(4)) R1 (.D(D_IN), .en(and_2_out), .clk(CLK), .Q(R1_q));  // open: clr
  buf and_2 (and_2_out, decoder_1_out1);  // AND_Gate
  Register #(.width(4)) R2 (.D(D_IN), .en(and_3_out), .clk(CLK), .Q(R2_q));  // open: clr
  buf and_3 (and_3_out, decoder_1_out2);  // AND_Gate
  Register #(.width(4)) R3 (.D(D_IN), .en(and_4_out), .clk(CLK), .Q(R3_q));  // open: clr
  buf and_4 (and_4_out, decoder_1_out3);  // AND_Gate
  Register #(.width(4)) R4 (.D(D_IN), .en(and_5_out), .clk(CLK), .Q(R4_q));  // open: clr
  and and_5 (and_5_out, decoder_1_out4, RW);
  Register #(.width(4)) R5 (.D(D_IN), .en(and_6_out), .clk(CLK), .Q(R5_q));  // open: clr
  and and_6 (and_6_out, decoder_1_out5, RW);
  Register #(.width(4)) R6 (.D(D_IN), .en(and_7_out), .clk(CLK), .Q(R6_q));  // open: clr
  and and_7 (and_7_out, decoder_1_out6, RW);
  Register #(.width(4)) R7 (.D(D_IN), .en(and_8_out), .clk(CLK), .Q(R7_q));  // open: clr
  and and_8 (and_8_out, decoder_1_out7, RW);
  Multiplexer #(.select(3), .width(4)) multiplexer_1 (
    .in0(R0_q), .in1(R1_q), .in2(R2_q), .in3(R3_q), .in4(R4_q), .in5(R5_q), .in6(R6_q), .in7(R7_q),
    .out(AOut), .sel(AA));
  Decoder #(.enable("false"), .select(3)) decoder_2 (
    .out0(decoder_2_out0), .out1(decoder_2_out1), .out2(decoder_2_out2), .out3(decoder_2_out3),
    .out4(decoder_2_out4), .out5(decoder_2_out5), .out6(decoder_2_out6), .out7(decoder_2_out7), .sel(DA));
  buf and_9 (and_9_out, decoder_2_out0);  // AND_Gate
  buf and_10 (and_10_out, decoder_2_out1);  // AND_Gate
  buf and_11 (and_11_out, decoder_2_out2);  // AND_Gate
  buf and_12 (and_12_out, decoder_2_out3);  // AND_Gate
  buf and_13 (and_13_out, decoder_2_out4);  // AND_Gate
  buf and_14 (and_14_out, decoder_2_out5);  // AND_Gate
  buf and_15 (and_15_out, decoder_2_out6);  // AND_Gate
  buf and_16 (and_16_out, decoder_2_out7);  // AND_Gate
  Register #(.width(4)) register_1 (.D(D_IN), .en(and_9_out), .clk(CLK), .Q(register_1_q));  // open: clr
  Register #(.width(4)) register_2 (.D(D_IN), .en(and_10_out), .clk(CLK), .Q(register_2_q));  // open: clr
  Register #(.width(4)) register_3 (.D(D_IN), .en(and_11_out), .clk(CLK), .Q(register_3_q));  // open: clr
  Register #(.width(4)) register_4 (.D(D_IN), .en(and_12_out), .clk(CLK), .Q(register_4_q));  // open: clr
  Register #(.width(4)) register_5 (.D(D_IN), .en(and_13_out), .clk(CLK), .Q(register_5_q));  // open: clr
  Register #(.width(4)) register_6 (.D(D_IN), .en(and_14_out), .clk(CLK), .Q(register_6_q));  // open: clr
  Register #(.width(4)) register_7 (.D(D_IN), .en(and_15_out), .clk(CLK), .Q(register_7_q));  // open: clr
  Register #(.width(4)) register_8 (.D(D_IN), .en(and_16_out), .clk(CLK), .Q(register_8_q));  // open: clr
  Multiplexer #(.select(3), .width(4)) multiplexer_2 (
    .in0(register_1_q), .in1(register_2_q), .in2(register_3_q), .in3(register_4_q), .in4(register_5_q),
    .in5(register_6_q), .in6(register_7_q), .in7(register_8_q), .out(BOut), .sel(BA));
endmodule

module function_unit (
  input  [3:0] a_in,
  input  [3:0] b_in,
  input  [3:0] FS,
  output [2:0] PZN,
  output [3:0] F
);

  wire [3:0] adder_1_out, adder_2_out, and_1_out, divider_1_out, multiplier_1_out, negator_1_out,
       negator_2_out, or_1_out, shifter_1_out, shifter_2_out, shifter_3_out, subtractor_1_out;

  Adder #(.width(4)) adder_1 (.a(a_in), .b(b_in), .out(adder_1_out));  // open: cin, cout
  Subtractor #(.width(4)) subtractor_1 (.a(a_in), .b(b_in), .out(subtractor_1_out));  // open: bin, bout
  Multiplier #(.width(4)) multiplier_1 (.a(a_in), .b(b_in), .out(multiplier_1_out));  // open: cin, cout
  Divider #(.mode("twosComplement"), .width(4)) divider_1 (
    .a(a_in), .b(b_in), .out(divider_1_out));  // open: upper, rem
  Negator #(.width(4)) negator_1 (.in(a_in), .out(negator_1_out));
  assign and_1_out = a_in & b_in;  // AND_Gate and_1, 4 bits wide
  assign or_1_out = a_in | b_in;  // OR_Gate or_1, 4 bits wide
  Negator #(.width(4)) negator_2 (.in(a_in), .out(negator_2_out));
  Shifter #(.shift("lr"), .width(4)) shifter_1 (.in(a_in), .\dist (2'b01), .out(shifter_1_out));
  Shifter #(.width(4)) shifter_2 (.in(a_in), .\dist (2'b01), .out(shifter_2_out));
  Shifter #(.shift("ar"), .width(4)) shifter_3 (.in(a_in), .\dist (2'b01), .out(shifter_3_out));
  Adder #(.width(4)) adder_2 (.a(negator_2_out), .b(4'b0001), .out(adder_2_out));  // open: cin, cout
  Multiplexer #(.select(4), .width(4)) multiplexer_1 (
    .in0(4'b0000), .in1(4'b0001), .in2(a_in), .in3(b_in), .in4(adder_1_out), .in5(subtractor_1_out),
    .in6(multiplier_1_out), .in7(divider_1_out), .in8(negator_1_out), .in9(and_1_out), .in10(or_1_out),
    .in11(adder_2_out), .in12(shifter_1_out), .in13(shifter_2_out), .in14(shifter_3_out), .out(F), .sel(FS));  // open: in15
  Comparator #(.width(4)) comparator_1 (.a(F), .b(4'b0000), .gt(PZN[2]), .eq(PZN[1]), .lt(PZN[0]));
endmodule
